# Fritzing sketch arduino (saved by Fritzing 0.8.5b)
breadboards: 1

parts:
  Composants1 = Arduino Mega 2560 (Rev3)
  J1 = Basic Servo
  J2 = Basic Servo
  R1 = Photocell (LDR) [package=THT]
  T1 = LM35 Temperature Sensor [package="TO92 [THT]"]
  R2 = Resistor [tolerance=±5% resistance=220 package=THT]
  VCC1 = Battery

nets:
  N1: Composants1.A9, T1.Vout
  N2: Composants1.A7, R1.pin_0, R2.Pin_1
  VCC: Composants1.5V, J1.vcc, J2.vcc, R1.pin_1, T1.+Vs
  GND: Composants1.GND, J1.gnd, J2.gnd, T1.GND, R2.Pin_0, VCC1.-
  N3: Composants1.VIN, VCC1.+
  N4: Composants1.D6_PWM, J1.pulse
  N5: Composants1.D7_PWM, J2.pulse
