# Fritzing sketch arduino2 (saved by Fritzing 0.8.5b)
breadboards: 1

parts:
  Composants1 = Arduino Mega 2560 (Rev3)
  J1 = Basic Servo
  J2 = Basic Servo
  R1 = Photocell (LDR) [package=THT]
  T1 = LM35 Temperature Sensor [package="TO92 [THT]"]
  R2 = Resistor [tolerance=±5% resistance=220 package=THT]
  VCC1 = Battery
  NRF24L3 = NRF24L01

nets:
  N1: Composants1.A9, T1.Vout
  N2: Composants1.A7, R1.pin_0, R2.Pin_1
  VCC: Composants1.5V, J1.vcc, J2.vcc, R1.pin_1, T1.+Vs, NRF24L3.VCC
  GND: Composants1.GND, J1.gnd, J2.gnd, T1.GND, R2.Pin_0, VCC1.-, NRF24L3.GND
  N3: Composants1.VIN, VCC1.+
  N4: Composants1.D6_PWM, J1.pulse
  N5: Composants1.D7_PWM, J2.pulse
  N6: Composants1.D40, NRF24L3.CE
  N7: Composants1.D50, NRF24L3.MISO
  N8: Composants1.D51, NRF24L3.MOSI
  N9: Composants1.D52, NRF24L3.SCK
  N10: Composants1.D53, NRF24L3.CSN

custom parts:
  NRF24L01: NRF24L01 module
